// Logisim project 4_bit_cpu.circ as structural Verilog: 4 circuits, main circuit ALU
module ALU (
  input  [3:0] A,
  input  [3:0] B,
  input  [3:0] OP,
  output [3:0] Y,
  output [3:0] HI,
  output C,
  output V,
  output N,
  output Z
);

  wire BORW, BZ, CADD, D3, NXAB, PHNZ, PHZ, S3, VADD, VSUB, XAB, XAD, XAS;
  wire [2:0] DIF, SUM;
  wire [3:0] AND4, OR4, PHI, PRO, QUO, remainder, XOR4;

  Divider #(.width(4)) divider_1 (.a(A), .b(B), .out(QUO), .upper(4'b0000), .rem(remainder));
  Comparator #(.mode("unsigned"), .width(4)) comparator_1 (.a({N, Y[2:0]}), .b(4'b0000), .eq(Z));  // open: gt, lt
  Comparator #(.mode("unsigned"), .width(4)) comparator_2 (.a(B), .b(4'b0000), .eq(BZ));  // open: gt, lt
  not not_1 (NXAB, XAB);
  Multiplexer #(.select(4)) multiplexer_1 (
    .in0(1'b0), .in1(1'b0), .in2(1'b0), .in3(CADD), .in4(BORW), .in5(PHNZ), .in6(1'b0), .in7(1'b0),
    .in8(1'b0), .in9(A[3]), .in10(A[0]), .in11(1'b0), .in12(1'b0), .in13(1'b0), .in14(1'b0), .in15(1'b0),
    .out(C), .sel(OP));
  assign AND4 = A & B;  // AND_Gate and_1, 4 bits wide
  xor xor_1 (XAS, A[3], S3);
  Multiplexer #(.select(4)) multiplexer_2 (
    .in0(1'b0), .in1(1'b0), .in2(1'b0), .in3(VADD), .in4(VSUB), .in5(1'b0), .in6(1'b0), .in7(1'b0),
    .in8(1'b0), .in9(1'b0), .in10(1'b0), .in11(BZ), .in12(1'b0), .in13(1'b0), .in14(1'b0), .in15(1'b0),
    .out(V), .sel(OP));
  assign OR4 = A | B;  // OR_Gate or_1, 4 bits wide
  Adder #(.width(4)) adder_1 (.a(A), .b(B), .out({S3, SUM}), .cin(1'b0), .cout(CADD));
  xor xor_2 (XAD, A[3], D3);
  Comparator #(.mode("unsigned"), .width(4)) comparator_3 (.a(A), .b(B), .lt(BORW));  // open: gt, eq
  Multiplexer #(.select(4), .width(4)) multiplexer_3 (
    .in0(4'b0000), .in1(4'b0000), .in2(4'b0000), .in3({S3, SUM}), .in4({D3, DIF}), .in5(PRO), .in6(AND4),
    .in7(OR4), .in8(XOR4), .in9({A[2:0], 1'b0}), .in10({1'b0, A[3:1]}), .in11(QUO), .in12(4'b0000),
    .in13(4'b0000), .in14(B), .in15(4'b0000), .out({N, Y[2:0]}), .sel(OP));
  Subtractor #(.width(4)) subtractor_1 (.a(A), .b(B), .out({D3, DIF}), .bin(1'b0));  // open: bout
  assign XOR4 = A ^ B;  // XOR_Gate xor_3, 4 bits wide
  Comparator #(.mode("unsigned"), .width(4)) comparator_4 (.a(PHI), .b(4'b0000), .eq(PHZ));  // open: gt, lt
  and and_2 (VADD, NXAB, XAS);
  Multiplier #(.width(4)) multiplier_1 (.a(A), .b(B), .out(PRO), .cin(4'b0000), .cout(PHI));
  Multiplexer #(.width(4)) multiplexer_4 (.in0(PHI), .in1(remainder), .out(HI), .sel(OP[3]));
  not not_2 (PHNZ, PHZ);
  xor xor_4 (XAB, A[3], B[3]);
  and and_3 (VSUB, XAB, XAD);

  assign Y[3] = N;

  // Other names for the same wires on the sheet: SHL[3:1] = A[2:0]; SHR[2:0] = A[3:1]; CF = C; DIF[3] = D3;
  //   HIOUT[3:0] = HI; SUM[3] = S3; VF = V; Y3 = N; ZF = Z

  // Notes on the sheet:
  //   OPCODE
  //   First operand
  //   Second operand
  //   Main result
  //   High part of result
  //   Overflow flag
  //   Negative/sign flag
  //   Carry flag
  //   Zero flag
  //   Left-shift result
  //   Division remainder
  //   Division quotient
  //   Right-shift result
  //   AND result
  //   OR result
  //   Addition result
  //   High-part data path
  //   XOR result
  //   Subtraction result
  //   Multiplication result
endmodule

module REGFILE (
  input  CLK,
  input  RST,
  input  [1:0] RD,
  input  [1:0] RS,
  input  [3:0] WD,
  input  WE,
  input  HIWE,
  input  [3:0] HID,
  input  HISEL,
  output [3:0] RA,
  output [3:0] RB,
  output [3:0] R0,
  output [3:0] R1,
  output [3:0] R2,
  output [3:0] R3,
  output [3:0] HI
);

  wire W0, W1, W2, W3;
  wire [3:0] RBR;

  Decoder #(.select(2)) decoder_1 (.out0(W0), .out1(W1), .out2(W2), .out3(W3), .sel(RD), .en(WE));
  Register #(.width(4)) register_1 (.D(HID), .en(HIWE), .clk(CLK), .Q(HI), .clr(RST));
  Register #(.width(4)) register_2 (.D(WD), .en(W0), .clk(CLK), .Q(R0), .clr(RST));
  Multiplexer #(.select(2), .width(4)) multiplexer_1 (.in0(R0), .in1(R1), .in2(R2), .in3(R3), .out(RA), .sel(RD));
  Register #(.width(4)) register_3 (.D(WD), .en(W1), .clk(CLK), .Q(R1), .clr(RST));
  Multiplexer #(.select(2), .width(4)) multiplexer_2 (.in0(R0), .in1(R1), .in2(R2), .in3(R3), .out(RBR), .sel(RS));
  Register #(.width(4)) register_4 (.D(WD), .en(W2), .clk(CLK), .Q(R2), .clr(RST));
  Multiplexer #(.width(4)) multiplexer_3 (.in0(RBR), .in1(HI), .out(RB), .sel(HISEL));
  Register #(.width(4)) register_5 (.D(WD), .en(W3), .clk(CLK), .Q(R3), .clr(RST));

  // Notes on the sheet:
  //   Register destination selection
  //   Register source selection
  //   Data to write
  //   Register write enable
  //   HI write enable
  //   Data sent to HI
  //   HI selection
  //   Reset
  //   General purpose register 0
  //   General purpose register 1
  //   General purpose register 2
  //   General purpose register 3
  //   High register
  //   First register read data
  //   Second register read data
endmodule

module CONTROL (
  input  [3:0] OP,
  input  IB0,
  input  T,
  input  ZF,
  output RWE,
  output RAMWE,
  output [1:0] WBSEL,
  output HIWE,
  output FLGWE,
  output PCLOAD,
  output HALT,
  output HISEL
);

  wire C_FLG, C_HIWE, C_JMP, C_JZ, C_MOV, C_RAMWE, C_RW, JTAKEN, JZT;

  ROM #(.addrWidth(4), .dataWidth(10)) rom_1 (
    .addr(OP), .data({C_MOV, HALT, C_JZ, C_JMP, C_FLG, C_HIWE, WBSEL, C_RAMWE, C_RW}));
  and and_1 (FLGWE, C_FLG, T);
  and and_2 (JZT, C_JZ, ZF);
  or or_1 (JTAKEN, C_JMP, JZT);
  and and_3 (RWE, C_RW, T);
  and and_4 (PCLOAD, JTAKEN, T);
  and and_5 (RAMWE, C_RAMWE, T);
  and and_6 (HIWE, C_HIWE, T);
  and and_7 (HISEL, C_MOV, IB0);

  // Other names for the same wires on the sheet: CTL[9:0] = {C_MOV, HALT, C_JZ, C_JMP, C_FLG, C_HIWE, WBSEL, C_RAMWE, C_RW}

  // Notes on the sheet:
  //   Operation/instruction code
  //   Instruction bit
  //   Timing/state signal
  //   Zero flag
  //   Program Counter Load(Loads a new PC value)
  //   Register Write Enable(Enables register writing)
  //   RAM Write Enable(Enables RAM writing)
  //   Write Back Select(Selects data written to registers)
  //   High Register Write Enable(Enables HI register writing)
  //   Flag Write Enable(Enables flag updates)
  //   HALT
  //   High Register Select(Selects high-register data)
  //   contents of rom_1 (hex, n*v repeats v):
  //   5 2 9 21 21 31 5*21 31 40 80 201 100
  //   Control word from ROM
  //   Conditional jump indication
  //   Register write control
  //   Write-back selection
  //   Flag control
  //   Conditional jump control
  //   Move control
  //   RAM write control
  //   HI write control
  //   Jump control
  //   Jump-taken indication
endmodule

module CPU (
  input  RST
);

  wire CALU, CF, CLK, FLGWE, HALT, HISEL, HIWE, NHALT, NT, PCEN, PCLOAD, RAMWE, RWE, T;
  wire [1:0] WBSEL;
  wire [3:0] ALUY, FLAGS, HI, HID, HLAGD, IMM, R0, R1, R2, R3, RA, RAMD, RB, WD;
  wire [3:1] FLAGD;
  wire [5:0] PC, PCN, PCP1;
  wire [11:0] ROMD;
  wire [11:4] IR;

  Hex_Digit_Display hex_digit_display_1 (.value(R0));  // open: dp
  Hex_Digit_Display hex_digit_display_2 (.value(R1));  // open: dp
  Hex_Digit_Display hex_digit_display_3 (.value(R2));  // open: dp
  // Probe on PC
  // Probe on {IR, IMM}
  // Probe on T
  // Probe on IR[11:8]
  // Probe on IR[7:6]
  // Probe on IR[5:4]
  // Probe on IMM
  // Probe on R0
  // Probe on R1
  // Probe on R2
  // Probe on R3
  // Probe on HI
  // Probe on HALT
  Hex_Digit_Display hex_digit_display_4 (.value(R3));  // open: dp
  Hex_Digit_Display hex_digit_display_5 (.value(HI));  // open: dp
  Clock u_CLK (.out(CLK));
  Register #(.width(1)) register_1 (.D(NT), .en(NHALT), .clk(CLK), .Q(T), .clr(RST));
  Multiplexer #(.width(6)) multiplexer_1 (.in0(PCP1), .in1({IR[5:4], IMM}), .out(PCN), .sel(PCLOAD));
  Multiplexer #(.select(2), .width(4)) multiplexer_2 (
    .in0(ALUY), .in1(RAMD), .in2(IMM), .in3(4'b0000), .out(WD), .sel(WBSEL));
  RAM #(.addrWidth(4), .dataWidth(4)) ram_1 (.addr(IMM), .we(RAMWE), .oe(1'b1), .clk(CLK), .din(RA), .dout(RAMD));
  not not_1 (NT, T);
  or or_1 (PCEN, NT, PCLOAD);
  ROM #(.addrWidth(6), .dataWidth(12)) rom_1 (.addr(PC), .data(ROMD));
  not not_2 (NHALT, HALT);
  CONTROL control_1 (
    .OP(IR[11:8]), .IB0(IMM[0]), .T(T), .ZF(FLAGS[0]), .RWE(RWE), .RAMWE(RAMWE), .WBSEL(WBSEL), .HIWE(HIWE),
    .FLGWE(FLGWE), .PCLOAD(PCLOAD), .HALT(HALT), .HISEL(HISEL));
  Register #(.width(6)) register_2 (.D(PCN), .en(PCEN), .clk(CLK), .Q(PC), .clr(RST));
  Register #(.width(12)) register_3 (.D(ROMD), .en(NT), .clk(CLK), .Q({IR, IMM}), .clr(RST));
  Register #(.width(4)) register_4 (
    .D({FLAGD, CALU}), .en(FLGWE), .clk(CLK), .Q({FLAGS[3:2], CF, FLAGS[0]}), .clr(RST));
  REGFILE regfile_1 (
    .CLK(CLK), .RST(RST), .RD(IR[7:6]), .RS(IR[5:4]), .WD(WD), .WE(RWE), .HIWE(HIWE), .HID(HID),
    .HISEL(HISEL), .RA(RA), .RB(RB), .R0(R0), .R1(R1), .R2(R2), .R3(R3), .HI(HI));
  Adder #(.width(6)) adder_1 (.a(PC), .b(6'b000001), .out(PCP1), .cin(1'b0));  // open: cout
  Register #(.width(4)) register_5 (.D(HLAGD), .en(FLGWE), .clk(CLK), .Q({FLAGS[3:2], CF, FLAGS[0]}), .clr(RST));
  ALU alu_1 (.A(RA), .B(RB), .OP(IR[11:8]), .Y(ALUY), .HI(HID), .C(CALU), .V(FLAGD[3]), .N(FLAGD[2]), .Z(FLAGD[1]));
  // Probe on {FLAGS[3:2], CF, FLAGS[0]}
  // Probe on RA
  // Probe on RB
  // Probe on ALUY
  // Probe on IMM
  // Probe on RA
  // Probe on RAMD
  // Probe on RAMWE

  // Other names for the same wires on the sheet: FLAGD[0] = CALU; ZALU = FLAGD[1]; NALU = FLAGD[2]; VALU = FLAGD[3];
  //   ZF = FLAGS[0]; FLAGS[1] = CF; NF = FLAGS[2]; VF = FLAGS[3]; IR[3:0] = IMM; TARGET[5:0] = {IR[5:4], IMM};
  //   RS[1:0] = IR[5:4]; RD[1:0] = IR[7:6]; OP[3:0] = IR[11:8]

  // Notes on the sheet:
  //   General purpose register 0
  //   General purpose register 1
  //   General purpose register 2
  //   Generalcpurpose register 3
  //   Timing/state
  //   High register
  //   Program counter
  //   Next/selected PC path
  //   Register write data
  //   Timing/state storage
  //   RAM write enable
  //   RAM data
  //   contents of rom_1 (hex, n*v repeats v):
  //   205 245 e41 f00 b10 f00 ec0 20f 24f 510 e81 ec0 20c 243 b10 610 710 810 203 900 a00 100 2c0 c0 400
  //   d1b 2ce c1d 2cd f00
  //   Flag data path
  //   Instruction ROM output
  //   Instruction address
  //   Current instruction
  //   Flag/data-path-related storage
  //   First register operand
  //   Second register operand
  //   Immediate data
  //   Data-path storage
  //   ALU result
  //   RAM data
  //   RAM write enable
endmodule
