// Logisim project vending_machine.circ as structural Verilog: 1 circuit, main circuit main
module main (
  input  coin_5,
  input  coin_10,
  input  reset,
  input  cancel,
  output [4:0] out_5,
  output [3:0] out_6,
  output out_7,
  output out_8,
  output [4:0] out_9,
  output out_10,
  output [3:0] out_11,
  output out_12,
  output out_13,
  output out_14,
  output out_15,
  output out_16
);

  wire CLK;
  wire [3:0] CONES, CTENS;
  wire [5:0] ADDRT, CN;
  wire [7:0] XN;
  wire [15:3] ADDRA;
  wire [28:21] ODATA;

  Clock u_CLK (.out(CLK));
  Hex_Digit_Display hex_digit_display_1 (.value(CTENS));  // open: dp
  Hex_Digit_Display hex_digit_display_2 (.value(CONES));  // open: dp
  Hex_Digit_Display hex_digit_display_3 (.value(ODATA[24:21]));  // open: dp
  LED led_1 (.in(out_12));
  Hex_Digit_Display hex_digit_display_4 (.value(ODATA[28:25]));  // open: dp
  ROM #(.dataWidth(29)) ROM_OUT (
    .addr(ADDRA[15:8]), .data({ODATA, CONES, CTENS, out_8, out_7, out_10, out_12, out_6, out_5}));
  LED led_2 (.in(out_12));
  ROM #(.addrWidth(16)) ROM_CTRL (.addr({ADDRA[15:8], reset, ADDRA[6:3], cancel, coin_10, coin_5}), .data(XN));
  ROM #(.dataWidth(7)) ROM_TIMER (.addr({ADDRA[15:14], ADDRT}), .data({ADDRA[6], CN}));
  Hex_Digit_Display hex_digit_display_5 (.value(CTENS));  // open: dp
  Hex_Digit_Display hex_digit_display_6 (.value(CONES));  // open: dp
  Hex_Digit_Display hex_digit_display_7 (.value(ODATA[24:21]));  // open: dp
  Register #(.width(3)) PREV (.D({cancel, coin_10, coin_5}), .clk(CLK), .Q(ADDRA[5:3]));  // open: en, clr
  Hex_Digit_Display hex_digit_display_8 (.value(ODATA[28:25]));  // open: dp
  Register STATE (.D(XN), .clk(CLK), .Q(ADDRA[15:8]));  // open: en, clr
  Register #(.width(6)) CNT (.D(CN), .clk(CLK), .Q(ADDRT));  // open: en, clr

  assign out_9 = out_5;
  assign out_11 = out_6;
  assign out_13 = out_12;
  assign out_14 = out_10;
  assign out_15 = out_7;
  assign out_16 = out_8;

  // Other names for the same wires on the sheet: ADDRA (some bits) = {reset, cancel, coin_10, coin_5}; COIN5 = coin_5;
  //   INB[2:0] = {cancel, coin_10, coin_5}; COIN10 = coin_10; PREVQ[2:0] = ADDRA[5:3]; XQ[7:0] = ADDRA[15:8];
  //   CQ[5:0] = ADDRT; ADDRT[7:6] = ADDRA[15:14]; SQ[1:0] = ADDRA[15:14]; CREDIT[4:0] = out_5;
  //   ODATA[20:0] = {CONES, CTENS, out_8, out_7, out_10, out_12, out_6, out_5}; RETURN_AMOUNT[3:0] = out_6;
  //   DISPENSE = out_12; REFUND = out_10; BUSY = out_7; ERROR = out_8; RTENS[3:0] = ODATA[24:21];
  //   RONES[3:0] = ODATA[28:25]; TDATA[6:0] = {ADDRA[6], CN}; T63 = ADDRA[6]

  // Notes on the sheet:
  //   CREDIT
  //   Inputs
  //   Generates clock pulses
  //   5 Rupee Coin
  //   10 Rupee Coin
  //   Reset evrything to zero
  //   Cancel the transcation
  //   Outputs
  //   RETURN AMOUNT
  //   contents of ROM_OUT (hex, n*v repeats v):
  //   0 1000 a0000a0 a0010a0 200140 201140 a2001e0 a2011e0 a0005 a1005 a0a00a5 a0a10a5 2a0145 2a1145
  //   a2a01e5 a2a11e5 200a 300a a0020aa a0030aa 20214a 20314a a2021ea a2031ea a200f a300f a0a20af a0a30af
  //   2a214f 2a314f a2a21ef a2a31ef 4014 5014 a0040b4 a0050b4 204154 205154 a2041f4 a2051f4 0 1000 a0000a0
  //   a0010a0 200140 201140 a2001e0 a2011e0 0 1000 a0000a0 a0010a0 200140 201140 a2001e0 a2011e0 0 1000
  //   a0000a0 a0010a0 200140 201140 a2001e0 a2011e0 a00 1a00 a000aa0 a001aa0 200b40 201b40 a200be0 a201be0
  //   a0a05 a1a05 a0a0aa5 a0a1aa5 2a0b45 2a1b45 a2a0be5 a2a1be5 2a0a 3a0a a002aaa a003aaa 202b4a 203b4a
  //   a202bea a203bea a2a0f a3a0f a0a2aaf a0a3aaf 2a2b4f 2a3b4f a2a2bef a2a3bef 4a14 5a14 a004ab4 a005ab4
  //   204b54 205b54 a204bf4 a205bf4 a00 1a00 a000aa0 a001aa0 200b40 201b40 a200be0 a201be0 a00 1a00
  //   a000aa0 a001aa0 200b40 201b40 a200be0 a201be0 a00 1a00 a000aa0 a001aa0 200b40 201b40 a200be0 a201be0
  //   c00 1c00 a000ca0 a001ca0 200d40 201d40 a200de0 a201de0 a0c05 a1c05 a0a0ca5 a0a1ca5 2a0d45 2a1d45
  //   a2a0de5 a2a1de5 2c0a 3c0a a002caa a003caa 202d4a 203d4a a202dea a203dea a2c0f a3c0f a0a2caf a0a3caf
  //   2a2d4f 2a3d4f a2a2def a2a3def 4c14 5c14 a004cb4 a005cb4 204d54 205d54 a204df4 a205df4 c00 1c00
  //   a000ca0 a001ca0 200d40 201d40 a200de0 a201de0 c00 1c00 a000ca0 a001ca0 200d40 201d40 a200de0 a201de0
  //   c00 1c00 a000ca0 a001ca0 200d40 201d40 a200de0 a201de0 800 1800 a0008a0 a0018a0 200940 201940
  //   a2009e0 a2019e0 a0805 a1805 a0a08a5 a0a18a5 2a0945 2a1945 a2a09e5 a2a19e5 280a 380a a0028aa a0038aa
  //   20294a 20394a a2029ea a2039ea a280f a380f a0a28af a0a38af 2a294f 2a394f a2a29ef a2a39ef 4814 5814
  //   a0048b4 a0058b4 204954 205954 a2049f4 a2059f4 800 1800 a0008a0 a0018a0 200940 201940 a2009e0 a2019e0
  //   800 1800 a0008a0 a0018a0 200940 201940 a2009e0 a2019e0 800 1800 a0008a0 a0018a0 200940 201940
  //   a2009e0 a2019e0
  //   decodes STATE into CREDIT, RETURN_AMOUNT, indicators and 2-digit display values
  //   INB = {CANCEL,COIN10,COIN5}
  //   contents of ROM_CTRL (hex, n*v repeats v):
  //   0 8 10 1 6*0 10 10 5*0 8 0 8 13*0 8 10 1 0 8 10 1 0 0 10 10 0 0 10 10 0 8 0 8 0 8 0 8 9*0 8 10 1 6*0
  //   10 10 5*0 8 0 8 13*0 8 10 1 0 8 10 1 0 0 10 10 0 0 10 10 0 8 0 8 0 8 0 8 136*0 1 8 10 1 4*0 1 1 10
  //   10 4*0 1 8 1 8 4*0 4*1 4*0 1 8 10 1 1 8 10 1 1 1 10 10 1 1 10 10 1 8 1 8 1 8 1 8 9*1 8 10 1 4*0 1 1
  //   10 10 4*0 1 8 1 8 4*0 4*1 4*0 1 8 10 1 1 8 10 1 1 1 10 10 1 1 10 10 1 8 1 8 1 8 1 8 8*1 128*0 2 8 10
  //   3 6*2 10 10 5*2 8 2 8 13*2 8 10 3 2 8 10 3 2 2 10 10 2 2 10 10 2 8 2 8 2 8 2 8 9*2 8 10 3 6*2 10 10
  //   5*2 8 2 8 13*2 8 10 3 2 8 10 3 2 2 10 10 2 2 10 10 2 8 2 8 2 8 2 8 8*2 128*0 3 8 10 3 4*2 3 3 10 10
  //   4*2 3 8 3 8 4*2 4*3 4*2 3 8 10 3 3 8 10 3 3 3 10 10 3 3 10 10 3 8 3 8 3 8 3 8 9*3 8 10 3 4*2 3 3 10
  //   10 4*2 3 8 3 8 4*2 4*3 4*2 3 8 10 3 3 8 10 3 3 3 10 10 3 3 10 10 3 8 3 8 3 8 3 8 8*3 128*0 4 8 10 5
  //   6*4 10 10 5*4 8 4 8 13*4 8 10 5 4 8 10 5 4 4 10 10 4 4 10 10 4 8 4 8 4 8 4 8 9*4 8 10 5 6*4 10 10
  //   5*4 8 4 8 13*4 8 10 5 4 8 10 5 4 4 10 10 4 4 10 10 4 8 4 8 4 8 4 8 8*4 128*0 5 8 10 5 4*4 5 5 10 10
  //   4*4 5 8 5 8 4*4 4*5 4*4 5 8 10 5 5 8 10 5 5 5 10 10 5 5 10 10 5 8 5 8 5 8 5 8 9*5 8 10 5 4*4 5 5 10
  //   10 4*4 5 8 5 8 4*4 4*5 4*4 5 8 10 5 5 8 10 5 5 5 10 10 5 5 10 10 5 8 5 8 5 8 5 8 8*5 640*0 8 10 58 9
  //   4*82 8 8 58 58 4*82 8 10 8 10 4*82 4*8 4*82 8 10 58 9 8 10 58 9 8 8 58 58 8 8 58 58 8 10 8 10 8 10 8
  //   10 9*8 10 58 9 4*82 8 8 58 58 4*82 8 10 8 10 4*82 4*8 4*82 8 10 58 9 8 10 58 9 8 8 58 58 8 8 58 58 8
  //   10 8 10 8 10 8 10 8*8 128*0 9 10 58 9 4*82 9 9 58 58 4*82 9 10 9 10 4*82 4*9 4*82 9 10 58 9 9 10 58
  //   9 9 9 58 58 9 9 58 58 9 10 9 10 9 10 9 10 9*9 10 58 9 4*82 9 9 58 58 4*82 9 10 9 10 4*82 4*9 4*82 9
  //   10 58 9 9 10 58 9 9 9 58 58 9 9 58 58 9 10 9 10 9 10 9 10 8*9 128*0 a 10 58 b 4*82 a a 58 58 4*82 a
  //   10 a 10 4*82 4*a 4*82 a 10 58 b a 10 58 b a a 58 58 a a 58 58 a 10 a 10 a 10 a 10 9*a 10 58 b 4*82 a
  //   a 58 58 4*82 a 10 a 10 4*82 4*a 4*82 a 10 58 b a 10 58 b a a 58 58 a a 58 58 a 10 a 10 a 10 a 10 8*a
  //   128*0 b 10 58 b 4*82 b b 58 58 4*82 b 10 b 10 4*82 4*b 4*82 b 10 58 b b 10 58 b b b 58 58 b b 58 58
  //   b 10 b 10 b 10 b 10 9*b 10 58 b 4*82 b b 58 58 4*82 b 10 b 10 4*82 4*b 4*82 b 10 58 b b 10 58 b b b
  //   58 58 b b 58 58 b 10 b 10 b 10 b 10 8*b 128*0 c 10 58 d 4*82 c c 58 58 4*82 c 10 c 10 4*82 4*c 4*82
  //   c 10 58 d c 10 58 d c c 58 58 c c 58 58 c 10 c 10 c 10 c 10 9*c 10 58 d 4*82 c c 58 58 4*82 c 10 c
  //   10 4*82 4*c 4*82 c 10 58 d c 10 58 d c c 58 58 c c 58 58 c 10 c 10 c 10 c 10 8*c 128*0 d 10 58 d
  //   4*82 d d 58 58 4*82 d 10 d 10 4*82 4*d 4*82 d 10 58 d d 10 58 d d d 58 58 d d 58 58 d 10 d 10 d 10 d
  //   10 9*d 10 58 d 4*82 d d 58 58 4*82 d 10 d 10 4*82 4*d 4*82 d 10 58 d d 10 58 d d d 58 58 d d 58 58 d
  //   10 d 10 d 10 d 10 8*d 640*0 10 58 62 11 4*84 10 10 62 62 4*84 10 58 10 58 4*84 4*10 4*84 10 58 62 11
  //   10 58 62 11 10 10 62 62 10 10 62 62 10 58 10 58 10 58 10 58 9*10 58 62 11 4*84 10 10 62 62 4*84 10
  //   58 10 58 4*84 4*10 4*84 10 58 62 11 10 58 62 11 10 10 62 62 10 10 62 62 10 58 10 58 10 58 10 58 8*10
  //   128*0 11 58 62 11 4*84 11 11 62 62 4*84 11 58 11 58 4*84 4*11 4*84 11 58 62 11 11 58 62 11 11 11 62
  //   62 11 11 62 62 11 58 11 58 11 58 11 58 9*11 58 62 11 4*84 11 11 62 62 4*84 11 58 11 58 4*84 4*11
  //   4*84 11 58 62 11 11 58 62 11 11 11 62 62 11 11 62 62 11 58 11 58 11 58 11 58 8*11 128*0 12 58 62 13
  //   4*84 12 12 62 62 4*84 12 58 12 58 4*84 4*12 4*84 12 58 62 13 12 58 62 13 12 12 62 62 12 12 62 62 12
  //   58 12 58 12 58 12 58 9*12 58 62 13 4*84 12 12 62 62 4*84 12 58 12 58 4*84 4*12 4*84 12 58 62 13 12
  //   58 62 13 12 12 62 62 12 12 62 62 12 58 12 58 12 58 12 58 8*12 128*0 13 58 62 13 4*84 13 13 62 62
  //   4*84 13 58 13 58 4*84 4*13 4*84 13 58 62 13 13 58 62 13 13 13 62 62 13 13 62 62 13 58 13 58 13 58 13
  //   58 9*13 58 62 13 4*84 13 13 62 62 4*84 13 58 13 58 4*84 4*13 4*84 13 58 62 13 13 58 62 13 13 13 62
  //   62 13 13 62 62 13 58 13 58 13 58 13 58 8*13 128*0 14 58 62 15 4*84 14 14 62 62 4*84 14 58 14 58 4*84
  //   4*14 4*84 14 58 62 15 14 58 62 15 14 14 62 62 14 14 62 62 14 58 14 58 14 58 14 58 9*14 58 62 15 4*84
  //   14 14 62 62 4*84 14 58 14 58 4*84 4*14 4*84 14 58 62 15 14 58 62 15 14 14 62 62 14 14 62 62 14 58 14
  //   5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
  //   contents of ROM_TIMER (hex, n*v repeats v):
  //   63*0 40 1 2 3 4 5 6 7 8 9 a b c d e f 10 11 12 13 14 15 16 17 18 19 1a 1b 1c 1d 1e 1f 20 21 22 23 24
  //   25 26 27 28 29 2a 2b 2c 2d 2e 2f 30 31 32 33 34 35 36 37 38 39 3a 3b 3c 3d 3e 3f 40 1 2 3 4 5 6 7 8
  //   9 a b c d e f 10 11 12 13 14 15 16 17 18 19 1a 1b 1c 1d 1e 1f 20 21 22 23 24 25 26 27 28 29 2a 2b 2c
  //   2d 2e 2f 30 31 32 33 34 35 36 37 38 39 3a 3b 3c 3d 3e 3f 40 1 2 3 4 5 6 7 8 9 a b c d e f 10 11 12
  //   13 14 15 16 17 18 19 1a 1b 1c 1d 1e 1f 20 21 22 23 24 25 26 27 28 29 2a 2b 2c 2d 2e 2f 30 31 32 33
  //   34 35 36 37 38 39 3a 3b 3c 3d 3e 3f 40
  //   Provides timer-related lookup values
  //   CREDIT
  //   next-state logic. Address = {STATE[8], RESET, T63, PREV[3], INB[3]}
  //   Stores a previous 3-bit value
  //   RETURN AMOUNT
  //   Stores the controller state
  //   Stores the counter value
endmodule
